# Fritzing sketch 4_3_schematic (saved by Fritzing 1.0.1rc)
breadboards: 1

parts:
  7_Segment1 = 7 Segment Display
  7_Segment2 = 7 Segment Display
  7_Segment3 = 7 Segment Display
  7_Segment4 = 7 Segment Display
  R1 = Resistor [tolerance=±5% power=0.25 resistance=100 package=THT]
  R2 = Resistor [tolerance=±5% power=0.25 resistance=100 package=THT]
  R3 = Resistor [tolerance=±5% power=0.25 resistance=100 package=THT]
  R4 = Resistor [tolerance=±5% power=0.25 resistance=100 package=THT]
  R5 = Resistor [tolerance=±5% power=0.25 resistance=100 package=THT]
  R7 = Resistor [tolerance=±5% power=0.25 resistance=100 package=THT]
  R8 = Resistor [tolerance=±5% power=0.25 resistance=100 package=THT]
  Компонент1 = Arduino Uno (Rev3)
  R9 = Resistor [tolerance=±5% power=0.25 resistance=4.7k package=THT]
  R10 = Resistor [tolerance=±5% power=0.25 resistance=4.7k package=THT]
  R11 = Resistor [tolerance=±5% power=0.25 resistance=4.7k package=THT]
  R12 = Resistor [tolerance=±5% power=0.25 resistance=4.7k package=THT]
  Q1 = PNP-Transistor [package="TO92 [THT]"]
  Q4 = PNP-Transistor [package="TO92 [THT]"]
  Q5 = PNP-Transistor [package="TO92 [THT]"]
  Q6 = PNP-Transistor [package="TO92 [THT]"]

nets:
  N1: 7_Segment1.Segment_G, 7_Segment2.Segment_G, 7_Segment3.Segment_G, 7_Segment4.Segment_G, R7.Pin_1
  N2: 7_Segment1.Segment_F, 7_Segment1.Segment_B, 7_Segment2.Segment_F, 7_Segment2.Segment_B, 7_Segment3.Segment_F, 7_Segment3.Segment_B, 7_Segment4.Segment_F, 7_Segment4.Segment_B, R2.Pin_1, R8.Pin_1
  N3: 7_Segment1.common_anode, Q1.C
  N4: 7_Segment1.Segment_E, 7_Segment2.Segment_E, 7_Segment3.Segment_E, 7_Segment4.Segment_E, R5.Pin_1
  N5: 7_Segment1.Segment_D, 7_Segment2.Segment_D, 7_Segment3.Segment_D, 7_Segment4.Segment_D, R3.Pin_1
  N6: 7_Segment1.Segment_C, 7_Segment2.Segment_C, 7_Segment3.Segment_C, 7_Segment4.Segment_C, R4.Pin_1
  N7: 7_Segment1.Segment_A, 7_Segment2.Segment_A, 7_Segment3.Segment_A, 7_Segment4.Segment_A, R1.Pin_1
  N8: 7_Segment2.common_anode, Q4.C
  N9: 7_Segment3.common_anode, Q5.C
  N10: 7_Segment4.common_anode, Q6.C
  N11: R1.Pin_0, Компонент1.D12/MISO
  N12: R2.Pin_0, Компонент1.D11_PWM/MOSI
  N13: R3.Pin_0, Компонент1.D9_PWM
  N14: R4.Pin_0, Компонент1.D10_PWM/SS
  N15: R5.Pin_0, Компонент1.D8
  N16: R7.Pin_0, Компонент1.D6_PWM
  N17: R8.Pin_0, Компонент1.D7
  N18: Компонент1.D2, R12.Pin_0
  N19: Компонент1.D3_PWM, R11.Pin_0
  N20: Компонент1.D4, R10.Pin_0
  N21: Компонент1.D5_PWM, R9.Pin_0
  N22: Компонент1.5V, Q1.E, Q4.E, Q5.E, Q6.E
  N23: R9.Pin_1, Q1.B
  N24: R10.Pin_1, Q4.B
  N25: R11.Pin_1, Q5.B
  N26: R12.Pin_1, Q6.B
