# Fritzing sketch 5_1_schematic (saved by Fritzing 1.0.1rc)

parts:
  Компонент1 = Arduino Uno (Rev3)
  R1 = Photocell (LDR) [package=THT]

nets:
  N1: Компонент1.A0, R1.pin_0
  N2: Компонент1.5V, R1.pin_1
