# Fritzing sketch 5_2_schematic (saved by Fritzing 1.0.1rc)

parts:
  Компонент1 = Arduino Uno (Rev3)
  LCD1 = LCD screen  # not connected
  Grove1 = Grove 3 Axis Digital Accelerometer 16g
  Компонент2 = Real Time Clock Module - DS1307 RTC Breakout Board

nets:
  N1: Компонент1.A4/SDA, Grove1.SDA
  N2: Компонент1.A5/SCL, Grove1.SCL
  N3: Компонент1.AREF, Компонент2.GND
  N4: Компонент1.D3_PWM, Компонент2.SDA
  N5: Компонент1.D4, Компонент2.SCL
  5V: Компонент1.5V, Grove1.VCC, Компонент2.5V
  GND: Компонент1.GND, Grove1.GND
